// Logisim project TP1Joao6551Samuel6553.circ as structural Verilog
module categorizacao (
  input  p3,
  input  p2,
  input  p1,
  input  p0,
  input  e1,
  input  e0,
  output c1,
  output c2,
  output c3,
  output E
);

  wire and_1_out, and_2_out, and_3_out, nor_2_out, not_1_out, not_2_out, not_3_out, or_1_out, or_2_out;

  not not_1 (not_1_out, e1);
  nor nor_1 (c1, p3, e1, e0);
  not not_2 (not_2_out, p3);
  not not_3 (not_3_out, p2);
  and and_1 (and_1_out, not_1_out, e0);
  or or_1 (or_1_out, p1, p0);
  and and_2 (and_2_out, p3, p2);
  nor nor_2 (nor_2_out, p1, p0);
  and and_3 (and_3_out, or_1_out, and_2_out);
  or or_2 (or_2_out, not_2_out, not_3_out, nor_2_out);
  and and_4 (c3, and_3_out, e1);
  and and_5 (c2, or_2_out, and_1_out);
  nor nor_3 (E, c1, c3, c2);
endmodule

module _7_segmentos (
  input  c3,
  input  c2,
  input  c1,
  input  Err,
  output out_5,
  output out_6,
  output out_7,
  output out_8,
  output out_9,
  output out_10,
  output out_11
);

  or or_1 (out_5, Err, c2, c3);
  or or_2 (out_7, Err, c3, c2);
  or or_3 (out_8, c1, c2, c3);
  or or_4 (out_9, Err, c2);
  or or_5 (out_10, c2, c3, Err);
  or or_6 (out_11, c1, c3);

  assign out_6 = Err;
endmodule

module circuito_completo (
  input  p3,
  input  p2,
  input  p1,
  input  p0,
  input  e1,
  input  e0
);

  wire categorizacao_1_c1, categorizacao_1_c2, categorizacao_1_c3, categorizacao_1_e, n7_segmentos_1_out_5,
       n7_segmentos_1_out_6, n7_segmentos_1_out_7, n7_segmentos_1_out_8, n7_segmentos_1_out_9,
       n7_segmentos_1_out_10, n7_segmentos_1_out_11;

  categorizacao categorizacao_1 (
    .p3(p3), .p2(p2), .p1(p1), .p0(p0), .e1(e1), .e0(e0), .c1(categorizacao_1_c1), .c2(categorizacao_1_c2),
    .c3(categorizacao_1_c3), .E(categorizacao_1_e));
  _7_segmentos u_7_segmentos_1 (
    .c3(categorizacao_1_c3), .c2(categorizacao_1_c2), .c1(categorizacao_1_c1), .Err(categorizacao_1_e),
    .out_5(n7_segmentos_1_out_5), .out_6(n7_segmentos_1_out_6), .out_7(n7_segmentos_1_out_7),
    .out_8(n7_segmentos_1_out_8), .out_9(n7_segmentos_1_out_9), .out_10(n7_segmentos_1_out_10),
    .out_11(n7_segmentos_1_out_11));
  _7_Segment_Display u_7_segment_display_1 (
    .g(n7_segmentos_1_out_5), .f(n7_segmentos_1_out_6), .a(n7_segmentos_1_out_7), .b(n7_segmentos_1_out_8),
    .e(n7_segmentos_1_out_9), .d(n7_segmentos_1_out_10), .c(n7_segmentos_1_out_11));  // open: dp
endmodule
